// Digital circuit CircuitTwo.dig as structural Verilog
module CircuitTwo (
  input  A,
  input  B,
  input  C,
  output F
);

  wire and_1_out, and_2_out, not_1_out;

  not not_1 (not_1_out, A);
  and and_1 (and_1_out, not_1_out, C);
  and and_2 (and_2_out, B, C);
  or or_1 (F, and_1_out, and_2_out);
endmodule
